# Fritzing sketch arduino-police-car (saved by Fritzing 0.9.3b)
breadboards: 1

parts:
  Part1 = Arduino Uno (Rev3)
  VCC1 = 4 x AAA Battery Mount
  M1 = DC Motor [part_number="Right Motor"]  # not connected
  M2 = DC Motor [part_number="Left Motor"]
  J1 = Basic Servo
  hc-sr1 = hc-sr04
  S1 = H-Bridge with L298N
  S2 = Pushbutton [package="[THT]"]
  R1 = Resistor [tolerance=±5% resistance=10k package="0402 [SMD]"]
  LED1 = LED - 5mm [color="Red (633nm)" package="5 mm [THT]"]
  R2 = Resistor [tolerance=±5% resistance=220 package="2010 [SMD]"]
  LED3 = LED - 5mm [color="Green (555nm)" package="5 mm [THT]"]
  LED4 = LED - 5mm [color="Blue (430nm)" package="5 mm [THT]"]
  R3 = Resistor [tolerance=±5% resistance=220 package="2010 [SMD]"]
  R4 = Resistor [tolerance=±5% resistance=220 package="2010 [SMD]"]

nets:
  N1: Part1.D9_PWM, J1.pulse
  N2: Part1.D10_PWM/SS, R2.Pin_1
  N3: Part1.D11_PWM/MOSI, R3.Pin_1
  N4: Part1.D12/MISO, hc-sr1.Echo
  N5: Part1.D13/SCK, hc-sr1.Trig
  N6: Part1.D2, S1.IN3
  N7: Part1.D3_PWM, S1.IN4
  N8: Part1.D4, S1.IN1
  N9: Part1.D5_PWM, S1.IN2
  N10: Part1.D6_PWM, S2.Pin_3, S2.Pin_4, R1.Pin_0
  N11: Part1.D7, R4.Pin_1
  VCC: Part1.5V, J1.vcc, hc-sr1.VCC, S2.Pin_1, S2.Pin_2
  GND: Part1.GND, J1.gnd, hc-sr1.GND, R1.Pin_1, LED1.cathode, LED3.cathode, LED4.cathode
  N12: VCC1.-, S1.GND
  N13: VCC1.+, S1.5V
  N14: M2.pin_1, S1.OUT4-Motor2
  N15: LED1.anode, R2.Pin_0
  N16: LED3.anode, R4.Pin_0
  N17: LED4.anode, R3.Pin_0

custom parts:
  H-Bridge with L298N: h-bridge
